// Digital circuit lab02_5.dig as structural Verilog
module lab02_5 (
  input  A,
  input  B,
  input  C,
  input  D,
  output Z1,
  output Z2,
  output Z3
);

  wire comparator_1_eq, comparator_2_eq, comparator_2_gt, comparator_2_lt, less1, less2, more1, more2;

  Comparator comparator_1 (.a(A), .b(C), .gt(more1), .eq(comparator_1_eq), .lt(less2));
  Comparator comparator_2 (.a(B), .b(D), .gt(comparator_2_gt), .eq(comparator_2_eq), .lt(comparator_2_lt));
  and and_1 (more2, comparator_2_gt, comparator_1_eq);
  and and_2 (Z3, comparator_2_eq, comparator_1_eq);
  and and_3 (less1, comparator_1_eq, comparator_2_lt);
  or or_1 (Z1, more1, more2);
  or or_2 (Z2, less1, less2);
endmodule
