// Digital circuit Lab03_3.dig as structural Verilog
module Lab03_3 (
  input  [3:0] In,
  input  [1:0] Selector
);

  wire A0, A1, A2, A3, S0, S1;

  not not_1 (A3, In[3]);
  not not_2 (A2, In[2]);
  not not_3 (A1, In[1]);
  not not_4 (A0, In[0]);
  not not_5 (S1, Selector[1]);
  not not_6 (S0, Selector[0]);

  // Other names for the same wires on the sheet: A0_t = In[0]; A1_t = In[1]; A2_t = In[2]; A3_t = In[3];
  //   S0_t = Selector[0]; S1_t = Selector[1]
endmodule
