// Digital circuit Lab03_4.dig as structural Verilog
module Lab03_4 (
  input  [6:0] In,
  output [6:0] Output
);

  wire and_1_out, and_2_out, and_3_out, and_4_out, and_5_out, and_6_out, and_7_out, c1, c2, c3, not_1_out,
       not_2_out, not_3_out, not_4_out, not_5_out, not_6_out, not_7_out, not_8_out, not_9_out;

  xor xor_1 (c1, In[3], In[2], In[1], In[0]);
  xor xor_2 (c2, In[5], In[4], In[1], In[0]);
  xor xor_3 (c3, In[6], In[4], In[2], In[0]);
  not not_1 (not_1_out, c1);
  not not_2 (not_2_out, c2);
  not not_3 (not_3_out, c1);
  not not_4 (not_4_out, c3);
  not not_5 (not_5_out, c1);
  not not_6 (not_6_out, c2);
  not not_7 (not_7_out, c3);
  not not_8 (not_8_out, c2);
  not not_9 (not_9_out, c3);
  and and_1 (and_1_out, not_1_out, not_2_out, c3);
  and and_2 (and_2_out, not_3_out, c2, not_4_out);
  and and_3 (and_3_out, not_5_out, c2, c3);
  and and_4 (and_4_out, c1, not_6_out, not_7_out);
  and and_5 (and_5_out, c1, not_8_out, c3);
  and and_6 (and_6_out, c1, c2, not_9_out);
  and and_7 (and_7_out, c1, c2, c3);
  xor xor_4 (Output[6], In[6], and_1_out);
  xor xor_5 (Output[5], In[5], and_2_out);
  xor xor_6 (Output[4], In[4], and_3_out);
  xor xor_7 (Output[3], In[3], and_4_out);
  xor xor_8 (Output[2], In[2], and_5_out);
  xor xor_9 (Output[1], In[1], and_6_out);
  xor xor_10 (Output[0], In[0], and_7_out);

  // Other names for the same wires on the sheet: m4 = In[0]; m3 = In[1]; m2 = In[2]; p3 = In[3]; m1 = In[4];
  //   p2 = In[5]; p1 = In[6]
endmodule
