// Digital circuit Template-04.dig as structural Verilog
module Template_04 (
  input  [6:0] In,
  output [6:0] Output
);

  wire and_1_out, and_2_out, and_3_out, and_4_out, and_5_out, and_6_out, c1, c2, c3, not_1_out, not_2_out,
       not_3_out;

  xor xor_1 (c1, In[3], In[2], In[1], In[0]);
  xor xor_2 (c2, In[5], In[4], In[1], In[0]);
  xor xor_3 (c3, In[6], In[4], In[2], In[0]);
  not not_1 (not_1_out, c1);
  not not_2 (not_2_out, c2);
  not not_3 (not_3_out, c3);
  and and_1 (and_1_out, not_1_out, not_2_out, c3);
  and and_2 (and_2_out, not_1_out, c2, not_3_out);
  and and_3 (and_3_out, not_1_out, c2, c3);
  and and_4 (and_4_out, c1, not_2_out, not_3_out);
  and and_5 (and_5_out, c1, not_2_out, c3);
  and and_6 (and_6_out, c1, c2, not_3_out);
  xor xor_4 (Output[6], and_1_out, In[6]);
  xor xor_5 (Output[5], and_2_out, In[5]);
  xor xor_6 (Output[4], and_3_out, In[4]);
  xor xor_7 (Output[3], and_4_out, In[3]);
  xor xor_8 (Output[2], and_5_out, In[2]);
  xor xor_9 (Output[1], and_6_out, In[1]);
  xor xor_10 (Output[0], In[0], 1'b0);

  // Other names for the same wires on the sheet: _7 = In[0]; _6 = In[1]; _5 = In[2]; _4 = In[3]; _3 = In[4];
  //   _2 = In[5]; _1 = In[6]
endmodule
