// Digital circuit Full_Adder.dig as structural Verilog
module Full_Adder (
  input  Cin,
  input  A,
  input  B,
  output Sum,
  output Cout
);

  wire nand_1_out, nand_2_out, nand_3_out, nand_4_out, nand_5_out, nand_6_out, nand_7_out;

  nand nand_1 (nand_1_out, A, B);
  nand nand_2 (nand_2_out, A, nand_1_out);
  nand nand_3 (nand_3_out, nand_1_out, B);
  nand nand_4 (nand_4_out, nand_2_out, nand_3_out);
  nand nand_5 (nand_5_out, nand_4_out, Cin);
  nand nand_6 (nand_6_out, nand_4_out, nand_5_out);
  nand nand_7 (nand_7_out, nand_5_out, Cin);
  nand nand_8 (Cout, nand_5_out, nand_1_out);
  nand nand_9 (Sum, nand_6_out, nand_7_out);

  // Other names for the same wires on the sheet: C = Cin
endmodule
