// Digital circuit Half_Adder.dig as structural Verilog
module Half_Adder (
  input  A,
  input  B,
  output Cout,
  output Sum
);

  wire nand_1_out, nand_2_out, nand_3_out;

  nand nand_1 (nand_1_out, A, B);
  nand nand_2 (nand_2_out, A, nand_1_out);
  nand nand_3 (nand_3_out, nand_1_out, B);
  nand nand_4 (Cout, nand_1_out, nand_1_out);
  nand nand_5 (Sum, nand_2_out, nand_3_out);
endmodule
