// Digital circuit Lab06.dig as structural Verilog
module Lab06 (
  input  [2:0] S,
  input  M,
  input  C,
  input  [3:0] A,
  input  [3:0] B,
  output [3:0] F
);

  wire and_2_out, and_3_out, and_4_out, and_5_out, and_6_out, and_8_out, and_9_out, and_10_out, and_11_out,
       and_12_out, and_13_out, and_14_out, and_15_out, and_16_out, and_17_out, and_18_out, not_1_out,
       not_2_out, not_4_out, not_5_out, not_6_out, not_7_out, not_9_out, not_10_out, not_11_out, not_12_out,
       not_13_out, not_14_out, S00, S01, S02, S03, S04, S05, S06, S07;
  wire [3:0] add_1_s, add_2_s, add_3_s, and_1_out, and_7_out, ari, barrelshifter_1_out, barrelshifter_2_out,
       Logic, nand_1_out, nor_1_out, not_3_out, not_8_out, or_1_out, sub_1_s, sub_2_s, sub_3_s, xnor_1_out;

  not not_1 (not_1_out, M);
  assign F = not_1_out ? Logic : 4'bz;  // Driver driver_1
  assign F = M ? ari : 4'bz;  // Driver driver_2
  LookUpTable lookuptable_1 (.in0(S[0]), .in1(S[1]), .in2(S[2]), .out(S00));
  LookUpTable lookuptable_2 (.in0(S[0]), .in1(S[1]), .in2(S[2]), .out(S01));
  LookUpTable lookuptable_3 (.in0(S[0]), .in1(S[1]), .in2(S[2]), .out(S02));
  LookUpTable lookuptable_4 (.in0(S[0]), .in1(S[1]), .in2(S[2]), .out(S03));
  LookUpTable lookuptable_5 (.in0(S[0]), .in1(S[1]), .in2(S[2]), .out(S04));
  LookUpTable lookuptable_6 (.in0(S[0]), .in1(S[1]), .in2(S[2]), .out(S05));
  LookUpTable lookuptable_7 (.in0(S[0]), .in1(S[1]), .in2(S[2]), .out(S06));
  LookUpTable lookuptable_8 (.in0(S[0]), .in1(S[1]), .in2(S[2]), .out(S07));
  not not_2 (not_2_out, M);
  assign not_3_out = ~A;  // Not not_3, 4 bits wide
  assign nand_1_out = ~(A & B);  // NAnd nand_1, 4 bits wide
  assign nor_1_out = ~(A | B);  // NOr nor_1, 4 bits wide
  assign xnor_1_out = ~(A ^ B);  // XNOr xnor_1, 4 bits wide
  assign and_1_out = A & B;  // And and_1, 4 bits wide
  assign or_1_out = A | B;  // Or or_1, 4 bits wide
  and and_2 (and_2_out, not_2_out, S00);
  not not_4 (not_4_out, M);
  not not_5 (not_5_out, M);
  not not_6 (not_6_out, M);
  not not_7 (not_7_out, M);
  assign not_8_out = ~B;  // Not not_8, 4 bits wide
  and and_3 (and_3_out, not_4_out, S01);
  and and_4 (and_4_out, not_5_out, S02);
  and and_5 (and_5_out, not_6_out, S03);
  and and_6 (and_6_out, not_7_out, S04);
  not not_9 (not_9_out, M);
  not not_10 (not_10_out, M);
  assign and_7_out = A & not_8_out;  // And and_7, 4 bits wide
  assign Logic = and_2_out ? not_3_out : 4'bz;  // Driver driver_3
  assign Logic = and_3_out ? nand_1_out : 4'bz;  // Driver driver_4
  assign Logic = and_4_out ? nor_1_out : 4'bz;  // Driver driver_5
  assign Logic = and_5_out ? xnor_1_out : 4'bz;  // Driver driver_6
  assign Logic = and_6_out ? and_1_out : 4'bz;  // Driver driver_7
  and and_8 (and_8_out, not_9_out, S05);
  and and_9 (and_9_out, not_10_out, S06);
  assign Logic = and_8_out ? or_1_out : 4'bz;  // Driver driver_8
  assign Logic = and_9_out ? and_7_out : 4'bz;  // Driver driver_9
  and and_10 (and_10_out, not_11_out, S07);
  not not_11 (not_11_out, M);
  assign Logic = and_10_out ? A : 4'bz;  // Driver driver_10
  and and_11 (and_11_out, M, S00);
  and and_12 (and_12_out, M, S01);
  and and_13 (and_13_out, M, S02);
  and and_14 (and_14_out, M, S03);
  and and_15 (and_15_out, M, S04);
  and and_16 (and_16_out, M, S05);
  and and_17 (and_17_out, M, S06);
  and and_18 (and_18_out, M, S07);
  BarrelShifter #(.Bits(4), .direction("right")) barrelshifter_1 (.in(A), .shift(3'b001), .out(barrelshifter_1_out));
  not not_12 (not_12_out, C);
  BarrelShifter #(.Bits(4)) barrelshifter_2 (.in(A), .shift(3'b001), .out(barrelshifter_2_out));
  Add #(.Bits(4)) add_1 (.a(A), .b(4'b0000), .c_i(C), .s(add_1_s));  // open: c_o
  Sub #(.Bits(4)) sub_1 (.a(A), .b(4'b0000), .c_i(not_12_out), .s(sub_1_s));  // open: c_o
  Add #(.Bits(4)) add_2 (.a(A), .b(B), .c_i(C), .s(add_2_s));  // open: c_o
  not not_13 (not_13_out, C);
  not not_14 (not_14_out, C);
  Sub #(.Bits(4)) sub_2 (.a(A), .b(B), .c_i(not_13_out), .s(sub_2_s));  // open: c_o
  Sub #(.Bits(4)) sub_3 (.a(4'b0000), .b(A), .c_i(not_14_out), .s(sub_3_s));  // open: c_o
  Add #(.Bits(4)) add_3 (.a(B), .b(4'b0000), .c_i(C), .s(add_3_s));  // open: c_o
  assign ari = and_17_out ? barrelshifter_2_out : 4'bz;  // Driver driver_11
  assign ari = and_18_out ? barrelshifter_1_out : 4'bz;  // Driver driver_12
  assign ari = and_11_out ? add_1_s : 4'bz;  // Driver driver_13
  assign ari = and_12_out ? sub_1_s : 4'bz;  // Driver driver_14
  assign ari = and_13_out ? add_2_s : 4'bz;  // Driver driver_15
  assign ari = and_14_out ? sub_2_s : 4'bz;  // Driver driver_16
  assign ari = and_15_out ? sub_3_s : 4'bz;  // Driver driver_17
  assign ari = and_16_out ? add_3_s : 4'bz;  // Driver driver_18

  // Other names for the same wires on the sheet: s2 = S[0]; s0 = S[2]

  // Notes on the sheet:
  //   contents of lookuptable_1 (hex, n*v repeats v):
  //   1
  //   contents of lookuptable_2 (hex, n*v repeats v):
  //   0,1
  //   contents of lookuptable_3 (hex, n*v repeats v):
  //   0,0,1
  //   contents of lookuptable_4 (hex, n*v repeats v):
  //   0,0,0,1
  //   contents of lookuptable_5 (hex, n*v repeats v):
  //   4*0,1
  //   contents of lookuptable_6 (hex, n*v repeats v):
  //   5*0,1
  //   contents of lookuptable_7 (hex, n*v repeats v):
  //   6*0,1
  //   contents of lookuptable_8 (hex, n*v repeats v):
  //   7*0,1
endmodule
