// Digital circuit Template.dig as structural Verilog
module Template (
  input  [3:0] A,
  input  [3:0] B,
  input  [2:0] S,
  input  M,
  input  C,
  input  [2:0] S_2,
  input  [2:0] S_3,
  input  [2:0] S_4,
  output [3:0] F
);

  wire add_1_s, add_2_s, add_3_s, add_4_s, add_5_s, add_6_s, add_7_s, add_8_s, add_9_s, add_10_s, add_11_s,
       add_12_s, add_13_s, add_14_s, add_15_s, add_16_s, and_1_out, and_2_out, and_6_out, and_7_out,
       and_11_out, and_12_out, and_16_out, and_17_out, Arithematic_C0, Arithematic_C1, b1, Cout_A, CoutA_1,
       CoutA_1_02, CoutA_B, CoutA_B_02, CoutA_plus_1, CoutA_plus_B, CoutA_plus_B_02, CoutA_plus_B_plus_1,
       CoutB_plus_1, Logical, multiplexer_1_out, multiplexer_2_out, multiplexer_3_out, multiplexer_4_out,
       multiplexer_5_out, multiplexer_6_out, multiplexer_7_out, multiplexer_8_out, multiplexer_9_out,
       multiplexer_10_out, multiplexer_11_out, multiplexer_12_out, nand_1_out, nand_2_out, nand_3_out,
       nand_4_out, nor_1_out, nor_2_out, nor_3_out, nor_4_out, not_1_out, not_2_out, not_3_out, not_4_out,
       not_5_out, not_6_out, not_7_out, not_8_out, not_9_out, not_10_out, not_11_out, not_12_out, not_13_out,
       not_14_out, not_15_out, not_16_out, or_1_out, or_2_out, or_3_out, or_4_out, sub_1_s, sub_2_s, sub_3_s,
       sub_4_s, sub_5_s, sub_6_s, sub_7_s, sub_8_s, sub_9_s, sub_10_s, sub_11_s, sub_12_s, undriven,
       undriven_2, undriven_3, xnor_1_out, xnor_2_out, xnor_3_out, xnor_4_out;

  not not_1 (not_1_out, b1);
  not not_2 (not_2_out, A[0]);
  nand nand_1 (nand_1_out, A[0], b1);
  nor nor_1 (nor_1_out, A[0], b1);
  xnor xnor_1 (xnor_1_out, A[0], b1);
  and and_1 (and_1_out, A[0], b1);
  or or_1 (or_1_out, A[0], b1);
  and and_2 (and_2_out, A[0], not_1_out);
  Sub sub_1 (.a(A[0]), .b(1'b1), .c_i(1'b1), .s(sub_1_s), .c_o(CoutA_1));
  Add add_1 (.a(A[0]), .b(b1), .c_i(1'b0), .s(add_1_s), .c_o(CoutA_plus_B));
  Sub sub_2 (.a(A[0]), .b(b1), .c_i(1'b1), .s(sub_2_s), .c_o(CoutA_B));
  Sub sub_3 (.a(A[0]), .b(1'b0), .c_i(1'b1), .s(sub_3_s), .c_o(Cout_A));
  Add add_2 (.a(A[0]), .b(1'b0), .c_i(1'b1), .s(add_2_s), .c_o(CoutA_plus_1));
  Add add_3 (.a(A[0]), .b(b1), .c_i(1'b1), .s(add_3_s), .c_o(CoutA_plus_B_plus_1));
  Add add_4 (.a(1'b0), .b(b1), .c_i(1'b1), .s(add_4_s), .c_o(CoutB_plus_1));
  Multiplexer #(.Selector_Bits(3)) multiplexer_1 (
    .sel(S), .in_0(not_2_out), .in_1(nand_1_out), .in_2(nor_1_out), .in_3(xnor_1_out), .in_4(and_1_out),
    .in_5(or_1_out), .in_6(and_2_out), .in_7(A[0]), .out(multiplexer_1_out));
  Multiplexer #(.Selector_Bits(3)) multiplexer_2 (
    .sel(S), .in_0(A[0]), .in_1(sub_1_s), .in_2(add_1_s), .in_3(sub_2_s), .in_4(sub_3_s), .in_5(b1),
    .in_6(1'b0), .in_7(1'b0), .out(multiplexer_2_out));
  Multiplexer #(.Selector_Bits(3)) multiplexer_3 (
    .sel(S), .in_0(add_2_s), .in_1(A[0]), .in_2(add_3_s), .in_3(sub_2_s), .in_4(sub_3_s), .in_5(add_4_s),
    .in_6(1'b0), .in_7(1'b0), .out(multiplexer_3_out));
  and and_3 (Logical, not_3_out, multiplexer_1_out);
  not not_3 (not_3_out, M);
  not not_4 (not_4_out, C);
  and and_4 (Arithematic_C0, not_4_out, M, multiplexer_2_out);
  and and_5 (Arithematic_C1, C, M, multiplexer_3_out);
  not not_5 (not_5_out, undriven);
  not not_6 (not_6_out, A[0]);
  nand nand_2 (nand_2_out, A[0], undriven);
  nor nor_2 (nor_2_out, A[0], undriven);
  xnor xnor_2 (xnor_2_out, A[0], undriven);
  and and_6 (and_6_out, A[0], undriven);
  or or_2 (or_2_out, A[0], undriven);
  and and_7 (and_7_out, A[0], not_5_out);
  Sub sub_4 (.a(A[0]), .b(1'b1), .c_i(CoutA_1), .s(sub_4_s), .c_o(CoutA_1_02));
  Add add_5 (.a(A[0]), .b(undriven), .c_i(CoutA_plus_B), .s(add_5_s), .c_o(CoutA_plus_B_02));
  Sub sub_5 (.a(A[0]), .b(undriven), .c_i(CoutA_B), .s(sub_5_s), .c_o(CoutA_B_02));
  Sub sub_6 (.a(A[0]), .b(1'b0), .c_i(1'b1), .s(sub_6_s), .c_o(Cout_A));
  Add add_6 (.a(A[0]), .b(1'b0), .c_i(1'b1), .s(add_6_s), .c_o(CoutA_plus_1));
  Add add_7 (.a(A[0]), .b(undriven), .c_i(1'b1), .s(add_7_s), .c_o(CoutA_plus_B_plus_1));
  Add add_8 (.a(1'b0), .b(undriven), .c_i(1'b1), .s(add_8_s), .c_o(CoutB_plus_1));
  Multiplexer #(.Selector_Bits(3)) multiplexer_4 (
    .sel(S), .in_0(not_6_out), .in_1(nand_2_out), .in_2(nor_2_out), .in_3(xnor_2_out), .in_4(and_6_out),
    .in_5(or_2_out), .in_6(and_7_out), .in_7(A[0]), .out(multiplexer_4_out));
  Multiplexer #(.Selector_Bits(3)) multiplexer_5 (
    .sel(S), .in_0(A[0]), .in_1(sub_4_s), .in_2(add_5_s), .in_3(sub_5_s), .in_4(sub_6_s), .in_5(undriven),
    .in_6(1'b0), .in_7(1'b0), .out(multiplexer_5_out));
  Multiplexer #(.Selector_Bits(3)) multiplexer_6 (
    .sel(S), .in_0(add_6_s), .in_1(A[0]), .in_2(add_7_s), .in_3(sub_5_s), .in_4(sub_6_s), .in_5(add_8_s),
    .in_6(1'b0), .in_7(1'b0), .out(multiplexer_6_out));
  and and_8 (Logical, not_7_out, multiplexer_4_out);
  not not_7 (not_7_out, M);
  and and_9 (Arithematic_C0, not_8_out, M, multiplexer_5_out);
  not not_8 (not_8_out, C);
  and and_10 (Arithematic_C1, C, M, multiplexer_6_out);
  not not_9 (not_9_out, A[0]);
  nand nand_3 (nand_3_out, A[0], undriven_2);
  nor nor_3 (nor_3_out, A[0], undriven_2);
  xnor xnor_3 (xnor_3_out, A[0], undriven_2);
  and and_11 (and_11_out, A[0], undriven_2);
  or or_3 (or_3_out, A[0], undriven_2);
  and and_12 (and_12_out, A[0], not_10_out);
  not not_10 (not_10_out, undriven_2);
  Sub sub_7 (.a(A[0]), .b(1'b1), .c_i(1'b1), .s(sub_7_s), .c_o(CoutA_1));
  Add add_9 (.a(A[0]), .b(undriven_2), .c_i(1'b0), .s(add_9_s), .c_o(CoutA_plus_B));
  Sub sub_8 (.a(A[0]), .b(undriven_2), .c_i(1'b1), .s(sub_8_s), .c_o(CoutA_B));
  Sub sub_9 (.a(A[0]), .b(1'b0), .c_i(1'b1), .s(sub_9_s), .c_o(Cout_A));
  Add add_10 (.a(A[0]), .b(1'b0), .c_i(1'b1), .s(add_10_s), .c_o(CoutA_plus_1));
  Add add_11 (.a(A[0]), .b(undriven_2), .c_i(1'b1), .s(add_11_s), .c_o(CoutA_plus_B_plus_1));
  Add add_12 (.a(1'b0), .b(undriven_2), .c_i(1'b1), .s(add_12_s), .c_o(CoutB_plus_1));
  Multiplexer #(.Selector_Bits(3)) multiplexer_7 (
    .sel(S), .in_0(not_9_out), .in_1(nand_3_out), .in_2(nor_3_out), .in_3(xnor_3_out), .in_4(and_11_out),
    .in_5(or_3_out), .in_6(and_12_out), .in_7(A[0]), .out(multiplexer_7_out));
  Multiplexer #(.Selector_Bits(3)) multiplexer_8 (
    .sel(S), .in_0(A[0]), .in_1(sub_7_s), .in_2(add_9_s), .in_3(sub_8_s), .in_4(sub_9_s), .in_5(undriven_2),
    .in_6(1'b0), .in_7(1'b0), .out(multiplexer_8_out));
  Multiplexer #(.Selector_Bits(3)) multiplexer_9 (
    .sel(S), .in_0(add_10_s), .in_1(A[0]), .in_2(add_11_s), .in_3(sub_8_s), .in_4(sub_9_s), .in_5(add_12_s),
    .in_6(1'b0), .in_7(1'b0), .out(multiplexer_9_out));
  not not_11 (not_11_out, M);
  not not_12 (not_12_out, C);
  and and_13 (Logical, not_11_out, multiplexer_7_out);
  and and_14 (Arithematic_C0, not_12_out, M, multiplexer_8_out);
  and and_15 (Arithematic_C1, C, M, multiplexer_9_out);
  not not_13 (not_13_out, undriven_3);
  not not_14 (not_14_out, A[0]);
  nand nand_4 (nand_4_out, A[0], undriven_3);
  nor nor_4 (nor_4_out, A[0], undriven_3);
  xnor xnor_4 (xnor_4_out, A[0], undriven_3);
  and and_16 (and_16_out, A[0], undriven_3);
  or or_4 (or_4_out, A[0], undriven_3);
  and and_17 (and_17_out, A[0], not_13_out);
  Sub sub_10 (.a(A[0]), .b(1'b1), .c_i(1'b1), .s(sub_10_s), .c_o(CoutA_1));
  Add add_13 (.a(A[0]), .b(undriven_3), .c_i(1'b0), .s(add_13_s), .c_o(CoutA_plus_B));
  Sub sub_11 (.a(A[0]), .b(undriven_3), .c_i(1'b1), .s(sub_11_s), .c_o(CoutA_B));
  Sub sub_12 (.a(A[0]), .b(1'b0), .c_i(1'b1), .s(sub_12_s), .c_o(Cout_A));
  Add add_14 (.a(A[0]), .b(1'b0), .c_i(1'b1), .s(add_14_s), .c_o(CoutA_plus_1));
  Add add_15 (.a(A[0]), .b(undriven_3), .c_i(1'b1), .s(add_15_s), .c_o(CoutA_plus_B_plus_1));
  Add add_16 (.a(1'b0), .b(undriven_3), .c_i(1'b1), .s(add_16_s), .c_o(CoutB_plus_1));
  Multiplexer #(.Selector_Bits(3)) multiplexer_10 (
    .sel(S), .in_0(not_14_out), .in_1(nand_4_out), .in_2(nor_4_out), .in_3(xnor_4_out), .in_4(and_16_out),
    .in_5(or_4_out), .in_6(and_17_out), .in_7(A[0]), .out(multiplexer_10_out));
  Multiplexer #(.Selector_Bits(3)) multiplexer_11 (
    .sel(S), .in_0(A[0]), .in_1(sub_10_s), .in_2(add_13_s), .in_3(sub_11_s), .in_4(sub_12_s),
    .in_5(undriven_3), .in_6(1'b0), .in_7(1'b0), .out(multiplexer_11_out));
  Multiplexer #(.Selector_Bits(3)) multiplexer_12 (
    .sel(S), .in_0(add_14_s), .in_1(A[0]), .in_2(add_15_s), .in_3(sub_11_s), .in_4(sub_12_s),
    .in_5(add_16_s), .in_6(1'b0), .in_7(1'b0), .out(multiplexer_12_out));
  and and_18 (Logical, not_15_out, multiplexer_10_out);
  not not_15 (not_15_out, M);
  and and_19 (Arithematic_C0, not_16_out, M, multiplexer_11_out);
  not not_16 (not_16_out, C);
  and and_20 (Arithematic_C1, C, M, multiplexer_12_out);

  assign F = 4'b0000;
  assign S_2 = S;
  assign S_3 = S;
  assign S_4 = S;

  // Other names for the same wires on the sheet: a1 = A[0]; A_t = A[0]; a2 = A[1]; a3 = A[2]; a4 = A[3]; b2 = B[1];
  //   b3 = B[2]; b4 = B[3]
endmodule
