// Digital circuit 03.dig as structural Verilog
module _03 (
  input  J,
  input  K,
  input  Clear,
  input  Clock,
  output Q,
  output Q_2
);

  wire and_1_out, and_2_out, and_3_out, and_4_out, nor_1_out, nor_2_out, nor_3_out, nor_4_out, not_1_out;

  and and_1 (and_1_out, nor_3_out, K, Clock);
  and and_2 (and_2_out, Clock, J, nor_4_out);
  nor nor_1 (nor_1_out, and_1_out, nor_2_out);
  nor nor_2 (nor_2_out, nor_1_out, and_2_out);
  and and_3 (and_3_out, nor_2_out, not_1_out);
  and and_4 (and_4_out, not_1_out, nor_1_out);
  not not_1 (not_1_out, Clock);
  nor nor_3 (nor_3_out, and_3_out, nor_4_out);
  nor nor_4 (nor_4_out, nor_3_out, and_4_out);
  and and_5 (Q, Clear, nor_3_out);
  or or_1 (Q_2, Clear, nor_4_out);
endmodule
