// Digital circuit Lab7_05.dig as structural Verilog
module Lab7_05 (
  input  T,
  input  Clear,
  input  Clock,
  output Q,
  output Q_2
);

  wire and_1_out, and_2_out, and_3_out, and_4_out, or_1_out;

  and and_1 (and_1_out, ~Clear, T);  // And
  and and_2 (and_2_out, Clear, Q);
  or or_1 (or_1_out, and_2_out, and_1_out);
  and and_3 (and_3_out, Q, or_1_out, Clock);
  and and_4 (and_4_out, Clock, or_1_out, Q_2);
  nor nor_1 (Q, and_3_out, Q_2);
  nor nor_2 (Q_2, Q, and_4_out);
endmodule
