// Digital circuit Lab08_2_newVersion.dig as structural Verilog
module Lab08_2_newVersion (
  input  A,
  input  B,
  input  Clr,
  input  Clock,
  output Z
);

  wire add_1_c_o, and_1_out, d_ff_1_q, driver_1_out, driver_2_out;

  assign driver_1_out = Clr ? A : 1'bz;  // Driver driver_1
  assign driver_2_out = Clr ? B : 1'bz;  // Driver driver_2
  Add add_1 (.a(driver_1_out), .b(driver_2_out), .c_i(d_ff_1_q), .s(Z), .c_o(add_1_c_o));
  D_FF d_ff_1 (.D(and_1_out), .C(Clock), .Q(d_ff_1_q));  // open: nQ
  and and_1 (and_1_out, add_1_c_o, Clr);
endmodule
