// Digital circuit Lab08_4.dig as structural Verilog
module Lab08_4 (
  input  P,
  input  Clr,
  input  clock,
  output Z
);

  wire and_1_out, and_2_out, d_ff_1_nq, d_ff_2_q, d_ff_3_q, not_1_out;

  and and_1 (and_1_out, d_ff_2_q, not_1_out);
  and and_2 (and_2_out, d_ff_3_q, not_1_out);
  not not_1 (not_1_out, Clr);
  D_FF d_ff_1 (.D(and_1_out), .C(clock), .nQ(d_ff_1_nq));  // open: Q
  D_FF d_ff_2 (.D(and_2_out), .C(clock), .Q(d_ff_2_q));  // open: nQ
  D_FF d_ff_3 (.D(P), .C(clock), .Q(d_ff_3_q));  // open: nQ
  and and_3 (Z, d_ff_1_nq, d_ff_2_q);
endmodule
