// Digital circuit Pre_Exam.dig as structural Verilog
module Pre_Exam (
  input  [2:0] in_1,
  input  [2:0] in_2
);

  wire _1, _2, _3, _4, _5, and_1_out, and_2_out, and_3_out, and_4_out, and_5_out, and_6_out, and_7_out,
       and_8_out, and_9_out, and_10_out, and_11_out, and_12_out, and_13_out, and_14_out, and_15_out,
       and_16_out, and_17_out, and_18_out, and_19_out, and_20_out, and_21_out, and_22_out, and_23_out,
       and_24_out, and_25_out, and_26_out, and_27_out, and_28_out, and_29_out, and_30_out, and_31_out,
       and_32_out, and_33_out, and_34_out, and_35_out, not_1_out, not_2_out, not_3_out, not_4_out, not_5_out,
       not_6_out, not_7_out, not_8_out, not_9_out, not_10_out, not_11_out, not_12_out, not_13_out;

  not not_1 (not_1_out, in_1[2]);
  not not_2 (not_2_out, in_1[1]);
  not not_3 (not_3_out, in_1[0]);
  not not_4 (not_4_out, in_2[2]);
  not not_5 (not_5_out, in_2[1]);
  not not_6 (not_6_out, in_2[0]);
  and and_1 (and_1_out, in_1[2], not_2_out, not_3_out, not_5_out, not_6_out);
  and and_2 (and_2_out, in_1[2], in_1[0], in_2[1], in_2[0]);
  and and_3 (and_3_out, in_1[2], in_1[1], in_1[0], in_2[0]);
  and and_4 (and_4_out, in_1[2], in_1[1], in_2[1]);
  and and_5 (and_5_out, in_1[2], in_2[2]);
  and and_6 (and_6_out, in_1[1], in_1[0], in_2[2], in_2[0]);
  and and_7 (and_7_out, in_1[1], in_2[2], in_2[1]);
  and and_8 (and_8_out, in_1[0], in_2[2], in_2[1], in_2[0]);
  and and_9 (and_9_out, not_1_out, in_1[0], not_4_out, in_2[1], in_2[0]);
  and and_10 (and_10_out, in_1[2], not_3_out, not_4_out, not_5_out, in_2[0]);
  and and_11 (and_11_out, in_1[2], in_1[0], in_2[2], in_2[1], in_2[0]);
  and and_12 (and_12_out, in_1[2], not_2_out, not_4_out, not_5_out, in_2[0]);
  and and_13 (and_13_out, in_1[2], in_1[1], not_4_out, not_5_out, not_6_out);
  and and_14 (and_14_out, not_1_out, in_1[1], in_1[0], not_4_out, in_2[0]);
  and and_15 (and_15_out, in_1[2], not_2_out, in_1[0], not_4_out, not_6_out);
  and and_16 (and_16_out, in_1[2], in_1[1], in_1[0], in_2[2], in_2[0]);
  and and_17 (and_17_out, in_1[2], not_2_out, not_3_out, not_4_out, in_2[1]);
  and and_18 (and_18_out, not_1_out, in_2[2], not_5_out, not_6_out);
  and and_19 (and_19_out, not_1_out, not_2_out, in_2[2], not_6_out);
  and and_20 (and_20_out, not_1_out, not_3_out, in_2[2], not_5_out);
  and and_21 (and_21_out, not_1_out, not_2_out, in_2[2], not_5_out);
  and and_22 (and_22_out, not_1_out, in_1[1], not_4_out, in_2[1]);
  and and_23 (and_23_out, in_1[2], in_1[1], in_2[2], in_2[1]);
  and and_24 (and_24_out, not_1_out, not_2_out, not_3_out, in_2[2]);
  and and_25 (and_25_out, not_2_out, not_3_out, in_2[1]);
  and and_26 (and_26_out, not_2_out, in_1[0], not_5_out, in_2[0]);
  and and_27 (and_27_out, not_2_out, in_2[1], not_6_out);
  and and_28 (and_28_out, in_1[1], not_3_out, not_5_out);
  and and_29 (and_29_out, in_1[1], not_5_out, not_6_out);
  and and_30 (and_30_out, in_1[1], in_1[0], in_2[1], in_2[0]);
  and and_31 (and_31_out, not_3_out, in_2[0]);
  and and_32 (and_32_out, in_1[0], not_6_out);
  or or_1 (_3, and_25_out, and_26_out, and_27_out, and_28_out, and_29_out, and_30_out);
  or or_2 (_4, and_31_out, and_32_out);
  or or_3 (_1, and_1_out, and_2_out, and_3_out, and_4_out, and_5_out, and_6_out, and_7_out, and_8_out);
  or or_4 (_2, and_9_out, and_10_out, and_11_out, and_12_out, and_13_out, and_14_out, and_15_out, and_16_out, and_17_out, and_18_out, and_19_out, and_20_out, and_21_out, and_22_out, and_23_out, and_24_out);
  not not_7 (not_7_out, _2);
  not not_8 (not_8_out, _3);
  not not_9 (not_9_out, _4);
  and and_33 (and_33_out, _1, not_8_out, _4);
  and and_34 (and_34_out, _1, _2, not_9_out);
  and and_35 (and_35_out, _1, not_7_out, _3);
  or or_5 (_5, and_33_out, and_34_out, and_35_out);
  not not_10 (not_10_out, _5);
  Seven_Seg seven_seg_1 (
    .a(not_10_out), .b(1'b1), .c(1'b1), .d(not_12_out), .e(not_11_out), .f(not_13_out), .g(1'b0), .dp(1'b0));
  not not_11 (not_11_out, _5);
  not not_12 (not_12_out, _5);
  not not_13 (not_13_out, _5);
endmodule
