// Digital circuit Pre_Exam2.dig as structural Verilog
module Pre_Exam2 (
  output O1,
  output O2
);

  wire _0, _1, _2, _3, _4, _5, _6, _7;
  wire [2:0] s0_out;

  DipSwitch s0 (.out(s0_out[2]));
  DipSwitch s1 (.out(s0_out[1]));
  DipSwitch s2 (.out(s0_out[0]));
  Decoder #(.Selector_Bits(3)) decoder_1 (
    .sel(s0_out), .out_0(_0), .out_1(_1), .out_2(_2), .out_3(_3), .out_4(_4), .out_5(_5), .out_6(_6),
    .out_7(_7));
  or or_1 (O1, _2, _4, _5, _6);
  or or_2 (O2, _0, _2, _4, _6, _7);
endmodule
