// Digital circuit Pre_Exam3.dig as structural Verilog
module Pre_Exam3 (
  input  [2:0] in0,
  input  addSubtract,
  input  [2:0] in1,
  output o3,
  output o2,
  output o1,
  output [2:0] F
);

  wire and_1_out, and_2_out, and_3_out, and_4_out, and_5_out, and_6_out, and_7_out, and_8_out, and_9_out,
       and_10_out, and_11_out, and_12_out, and_13_out, and_14_out, and_15_out, and_16_out, and_17_out,
       and_18_out, and_19_out, and_20_out, and_21_out, and_22_out, and_23_out, and_24_out, and_25_out,
       and_26_out, and_27_out, and_28_out, and_29_out, b1, b2, in0_1, in0_2, in1_3, in1_4, not_1_out,
       not_2_out, not_3_out, not_4_out, not_5_out, not_6_out, not_7_out, not_8_out, not_9_out, not_10_out,
       not_11_out, not_12_out, not_13_out, not_14_out, not_15_out, not_16_out, or_5_out, or_6_out, or_7_out,
       or_8_out, or_9_out, sub1, sub2, sub3;

  not not_1 (not_1_out, in1[2]);
  not not_2 (not_2_out, in1[1]);
  not not_3 (not_3_out, in1[0]);
  not not_4 (not_4_out, in0[2]);
  and and_1 (and_1_out, in1[2], in1[0]);
  and and_2 (and_2_out, in1[2], in1[1]);
  and and_3 (and_3_out, in1[1], in1[0]);
  and and_4 (and_4_out, not_1_out, not_2_out, in1[0]);
  and and_5 (and_5_out, not_1_out, in1[1], not_3_out);
  and and_6 (and_6_out, in1[2], not_2_out, not_3_out);
  and and_7 (and_7_out, in1[2], in1[1], in1[0]);
  not not_5 (not_5_out, in0[1]);
  not not_6 (not_6_out, in0[0]);
  or or_1 (in1_3, and_1_out, and_2_out, and_3_out);
  or or_2 (in1_4, and_4_out, and_5_out, and_6_out, and_7_out);
  and and_8 (and_8_out, in0[2], in0[0]);
  and and_9 (and_9_out, in0[2], in0[1]);
  and and_10 (and_10_out, in0[1], in0[0]);
  and and_11 (and_11_out, not_4_out, not_5_out, in0[0]);
  and and_12 (and_12_out, not_4_out, in0[1], not_6_out);
  and and_13 (and_13_out, in0[2], not_5_out, not_6_out);
  and and_14 (and_14_out, in0[2], in0[1], in0[0]);
  or or_3 (in0_1, and_8_out, and_9_out, and_10_out);
  or or_4 (in0_2, and_11_out, and_12_out, and_13_out, and_14_out);
  not not_7 (not_7_out, in0_1);
  not not_8 (not_8_out, in0_2);
  not not_9 (not_9_out, in0_2);
  not not_10 (not_10_out, in1_3);
  not not_11 (not_11_out, in1_4);
  not not_12 (not_12_out, in1_3);
  not not_13 (not_13_out, in1_4);
  and and_15 (and_15_out, in0_2, in1_3, in1_4);
  and and_16 (and_16_out, in0_2, in0_1, in1_4);
  and and_17 (and_17_out, in0_1, in1_3);
  and and_18 (and_18_out, not_8_out, not_7_out, in1_3);
  and and_19 (and_19_out, in0_2, not_7_out, not_10_out, in1_4);
  and and_20 (and_20_out, not_8_out, in0_1, not_10_out);
  and and_21 (and_21_out, in0_2, in0_1, in1_3, in1_4);
  and and_22 (and_22_out, not_7_out, in1_3, not_11_out);
  and and_23 (and_23_out, in0_1, not_10_out, not_11_out);
  and and_24 (and_24_out, not_8_out, in1_4);
  and and_25 (and_25_out, in0_2, not_11_out);
  and and_26 (and_26_out, in0_1, not_12_out, not_13_out);
  and and_27 (and_27_out, in0_1, in0_2, not_12_out);
  and and_28 (and_28_out, in0_2, not_13_out);
  and and_29 (and_29_out, not_9_out, in1_4);
  or or_5 (or_5_out, and_15_out, and_16_out, and_17_out);
  or or_6 (or_6_out, and_24_out, and_25_out);
  or or_7 (or_7_out, and_26_out, and_27_out);
  or or_8 (or_8_out, and_28_out, and_29_out);
  not not_14 (not_14_out, addSubtract);
  or or_9 (or_9_out, and_18_out, and_19_out, and_20_out, and_21_out, and_22_out, and_23_out);
  not not_15 (not_15_out, addSubtract);
  and and_30 (sub3, or_5_out, not_14_out);
  not not_16 (not_16_out, addSubtract);
  and and_31 (sub1, or_6_out, not_15_out);
  and and_32 (b2, or_7_out, addSubtract);
  and and_33 (b1, or_8_out, addSubtract);
  and and_34 (sub2, or_9_out, not_16_out);
  or or_10 (F[2], sub3, 1'b0);
  or or_11 (F[1], sub2, b2);
  or or_12 (F[0], sub1, b1);

  assign o1 = F[0];
  assign o2 = F[1];
  assign o3 = F[2];

  // Other names for the same wires on the sheet: sub = addSubtract
endmodule
